// Logisim project Digital assignment.circ as structural Verilog: 5 circuits, main circuit main
// Put the maximum number of your counter you want
module main (
);

  wire and_1_out, and_2_out, clock_1_out, controlled_buffer_1_out, decoder_for_mode_select_1_o1,
       decoder_for_mode_select_1_o2, decoder_for_mode_select_1_o3, decoder_for_mode_select_1_o4,
       keyboard_1_avail, not_1_out, not_2_out;
  wire [3:0] ascending_counter_logic_1_q4, ascending_counter_logic_1_q8, ascending_counter_logic_1_q12,
       controlled_buffer_5_out, register_1_q;
  wire [6:0] keyboard_1_data;

  assign controlled_buffer_1_out = keyboard_1_avail ? clock_1_out : 1'bz;  // Controlled_Buffer controlled_buffer_1
  Keyboard keyboard_1 (
    .clk(controlled_buffer_1_out), .re(1'b1), .clr(1'b0), .avail(keyboard_1_avail), .data(keyboard_1_data));
  Clock clock_1 (.out(clock_1_out));
  Register #(.width(4)) register_1 (
    .D(controlled_buffer_5_out), .en(1'b1), .Q(register_1_q), .clk(controlled_buffer_1_out));  // open: clr
  not not_1 (not_1_out, register_1_q[3]);
  and and_1 (and_1_out, not_1_out, register_1_q[0]);
  Hex_Digit_Display hex_digit_display_1 (.value(register_1_q));  // open: dp
  not not_2 (not_2_out, keyboard_1_data[6]);
  and and_2 (and_2_out, not_2_out, keyboard_1_data[4], keyboard_1_data[5]);
  assign controlled_buffer_5_out[3] = and_2_out ? keyboard_1_data[3] : 1'bz;  // Controlled_Buffer controlled_buffer_2
  assign controlled_buffer_5_out[2] = and_2_out ? keyboard_1_data[2] : 1'bz;  // Controlled_Buffer controlled_buffer_3
  assign controlled_buffer_5_out[1] = and_2_out ? keyboard_1_data[1] : 1'bz;  // Controlled_Buffer controlled_buffer_4
  assign controlled_buffer_5_out[0] = and_2_out ? keyboard_1_data[0] : 1'bz;  // Controlled_Buffer controlled_buffer_5
  decoder_for_mode_select decoder_for_mode_select_1 (
    .I1(register_1_q[2]), .I2(register_1_q[1]), .I3(and_1_out), .O1(decoder_for_mode_select_1_o1),
    .O2(decoder_for_mode_select_1_o2), .O3(decoder_for_mode_select_1_o3), .O4(decoder_for_mode_select_1_o4));
  Hex_Digit_Display hex_digit_display_2 (.value(ascending_counter_logic_1_q4));  // open: dp
  Hex_Digit_Display hex_digit_display_3 (.value(ascending_counter_logic_1_q8));  // open: dp
  Hex_Digit_Display hex_digit_display_4 (.value(ascending_counter_logic_1_q12));  // open: dp
  Ascending_counter_logic ascending_counter_logic_1 (
    .Q1(ascending_counter_logic_1_q4[3]), .Q2(ascending_counter_logic_1_q4[2]),
    .Q5(ascending_counter_logic_1_q8[3]), .Q6(ascending_counter_logic_1_q8[2]),
    .Q7(ascending_counter_logic_1_q8[1]), .Q8(ascending_counter_logic_1_q8[0]),
    .Q9(ascending_counter_logic_1_q12[3]), .Q10(ascending_counter_logic_1_q12[2]),
    .Q11(ascending_counter_logic_1_q12[1]), .Q12(ascending_counter_logic_1_q12[0]),
    .PRESET(decoder_for_mode_select_1_o2), .CLEAR(decoder_for_mode_select_1_o3),
    .HOLD_pin(decoder_for_mode_select_1_o4), .M(decoder_for_mode_select_1_o1),
    .Q4(ascending_counter_logic_1_q4[0]), .Q3(ascending_counter_logic_1_q4[1]));

  // Notes on the sheet:
  //   *Keyboard
  //   4 bit Register
  //   1 - Hold
  //   2 - Reset
  //   3 - Preset
  //   4 - Descending count
  //   5 - Descending hold
  //   0 or (6-9) - nothing has been selected
  //   decoder for selecting mode
  //   *Please type in the keyboard with number to select the mode
  //   Prefer 8 Hz (smoothly)
  //   up/down counter
endmodule

module decoder_for_7_segment_display (
  input  I1,
  input  I2,
  input  I3,
  input  I4,
  output a,
  output b,
  output c,
  output d,
  output e,
  output f,
  output g
);

  wire and_1_out, and_2_out, and_3_out, and_4_out, and_5_out, and_6_out, and_7_out, and_8_out, not_1_out,
       not_2_out, not_3_out, not_4_out, not_5_out, not_6_out, not_7_out, or_1_out, or_2_out, or_3_out,
       xnor_1_out, xor_1_out;

  not not_1 (not_1_out, I4);
  not not_2 (not_2_out, I1);
  not not_3 (not_3_out, I2);
  not not_4 (not_4_out, I4);
  or or_1 (or_1_out, not_3_out, I3);
  not not_5 (not_5_out, I3);
  not not_6 (not_6_out, I3);
  and and_1 (and_1_out, I2, I4);
  and and_2 (and_2_out, not_2_out, not_3_out, not_4_out);
  not not_7 (not_7_out, I2);
  or or_2 (or_2_out, not_6_out, not_1_out);
  xnor xnor_1 (xnor_1_out, I3, I4);
  and and_3 (and_3_out, not_3_out, I3);
  and and_4 (and_4_out, or_1_out, not_4_out);
  and and_5 (and_5_out, I2, not_5_out, I4);
  or or_3 (or_3_out, not_7_out, I3);
  and and_6 (and_6_out, I2, or_2_out);
  and and_7 (and_7_out, not_6_out, not_1_out);
  and and_8 (and_8_out, I3, not_1_out);
  xor xor_1 (xor_1_out, I2, I3);
  or or_4 (a, I1, I3, and_1_out, and_2_out);
  or or_5 (b, not_3_out, xnor_1_out);
  or or_6 (c, I1, I2, not_5_out, I4);
  or or_7 (d, I1, and_3_out, and_4_out, and_5_out);
  and and_9 (e, or_3_out, not_1_out);
  or or_8 (f, I1, and_6_out, and_7_out);
  or or_9 (g, I1, and_8_out, xor_1_out);
endmodule

module Ascending_counter_logic (
  input  M,
  input  PRESET,
  input  CLEAR,
  input  HOLD_pin,
  output Q4,
  output Q8,
  output Q3,
  output Q7,
  output Q12,
  output Q2,
  output Q6,
  output Q1,
  output Q11,
  output Q5,
  output Q10,
  output Q9
);

  wire and_1_out, and_2_out, and_3_out, and_4_out, and_5_out, and_6_out, and_7_out, and_8_out, and_9_out,
       and_10_out, and_11_out, and_12_out, and_13_out, and_14_out, and_15_out, and_16_out, and_17_out,
       and_18_out, and_19_out, and_20_out, and_21_out, and_22_out, and_23_out, and_24_out, and_25_out,
       and_26_out, and_27_out, and_28_out, and_29_out, CLOCK_out, not_1_out, not_2_out, not_3_out, not_4_out,
       not_5_out, not_6_out, not_7_out, not_8_out, not_9_out, not_10_out, not_11_out, not_12_out, not_13_out,
       not_14_out, not_15_out, not_16_out, not_17_out, not_18_out, not_19_out, not_20_out, not_21_out,
       not_22_out, not_23_out, not_24_out, not_25_out, not_26_out, not_27_out, not_28_out, not_29_out,
       not_30_out, not_31_out, not_32_out, not_33_out, not_34_out, not_35_out, not_36_out, not_37_out,
       not_38_out, not_39_out, not_40_out, not_41_out, not_42_out, not_43_out, not_44_out, not_45_out,
       not_46_out, not_47_out, not_48_out, not_49_out, not_50_out, not_51_out, or_1_out, or_2_out, or_3_out,
       or_4_out, or_5_out, or_6_out, or_7_out, or_8_out, or_9_out, or_10_out, or_11_out, or_12_out,
       or_13_out, or_14_out, or_15_out, or_16_out, or_17_out, or_18_out, xor_1_out, xor_2_out, xor_3_out,
       xor_4_out, xor_5_out, xor_6_out;

  or or_1 (or_1_out, and_1_out, and_2_out);
  J_K_Flip_Flop j_k_ff_1 (
    .J(or_1_out), .clk(CLOCK_out), .K(xor_1_out), .Q(Q1), .preset(PRESET), .en(and_15_out), .reset(CLEAR));  // open: Qn
  xor xor_1 (xor_1_out, M, Q4);
  or or_2 (or_2_out, PRESET, CLEAR);
  not not_1 (not_1_out, M);
  and and_1 (and_1_out, not_1_out, Q2, Q3, Q4);
  not not_2 (not_2_out, Q2);
  and and_2 (and_2_out, M, not_2_out, not_3_out, not_4_out);
  not not_3 (not_3_out, Q3);
  not not_4 (not_4_out, Q4);
  and and_3 (and_3_out, not_5_out, Q3, Q4);
  or or_3 (or_3_out, and_3_out, and_4_out);
  and and_4 (and_4_out, M, Q1, not_6_out);
  or or_4 (or_4_out, and_5_out, and_6_out);
  J_K_Flip_Flop j_k_ff_2 (
    .J(or_3_out), .clk(CLOCK_out), .K(or_4_out), .Q(Q2), .en(and_15_out), .reset(or_2_out));  // open: Qn, preset
  not not_5 (not_5_out, M);
  not not_6 (not_6_out, Q4);
  not not_7 (not_7_out, M);
  and and_5 (and_5_out, not_7_out, Q3, Q4);
  and and_6 (and_6_out, M, not_8_out, not_9_out);
  not not_8 (not_8_out, Q3);
  not not_9 (not_9_out, Q4);
  and and_7 (and_7_out, or_6_out, M, not_10_out);
  or or_5 (or_5_out, and_7_out, and_8_out);
  and and_8 (and_8_out, Q4, not_11_out, not_12_out);
  J_K_Flip_Flop j_k_ff_3 (
    .J(or_5_out), .clk(CLOCK_out), .K(xor_2_out), .Q(Q3), .en(and_15_out), .reset(or_2_out));  // open: Qn, preset
  xor xor_2 (xor_2_out, M, Q4);
  not not_10 (not_10_out, Q4);
  not not_11 (not_11_out, M);
  not not_12 (not_12_out, Q1);
  J_K_Flip_Flop j_k_ff_4 (
    .J(1'b1), .clk(CLOCK_out), .K(1'b1), .Q(Q4), .preset(PRESET), .en(and_15_out), .reset(CLEAR));  // open: Qn
  or or_6 (or_6_out, Q2, Q1);
  Hex_Digit_Display hex_digit_display_1 (.value({Q1, Q2, Q3, Q4}));  // open: dp
  xor xor_3 (xor_3_out, M, Q8);
  and and_9 (and_9_out, not_13_out, Q6, Q7, Q8);
  or or_7 (or_7_out, and_9_out, and_10_out);
  and and_10 (and_10_out, M, not_14_out, not_15_out, not_16_out);
  J_K_Flip_Flop j_k_ff_5 (
    .J(or_7_out), .clk(CLOCK_out), .K(xor_3_out), .Q(Q5), .preset(PRESET), .en(or_14_out), .reset(CLEAR));  // open: Qn
  or or_8 (or_8_out, and_11_out, and_12_out);
  or or_9 (or_9_out, and_13_out, and_14_out);
  not not_13 (not_13_out, M);
  not not_14 (not_14_out, Q6);
  not not_15 (not_15_out, Q7);
  not not_16 (not_16_out, Q8);
  J_K_Flip_Flop j_k_ff_6 (
    .J(or_8_out), .clk(CLOCK_out), .K(or_9_out), .Q(Q6), .en(or_14_out), .reset(or_2_out));  // open: Qn, preset
  not not_17 (not_17_out, M);
  and and_11 (and_11_out, not_17_out, Q7, Q8);
  and and_12 (and_12_out, M, Q5, not_18_out);
  not not_18 (not_18_out, Q8);
  not not_19 (not_19_out, M);
  and and_13 (and_13_out, not_19_out, Q7, Q8);
  and and_14 (and_14_out, M, not_20_out, not_21_out);
  not not_20 (not_20_out, Q7);
  not not_21 (not_21_out, Q8);
  and and_15 (and_15_out, or_11_out, or_14_out);
  or or_10 (or_10_out, and_16_out, and_17_out);
  J_K_Flip_Flop j_k_ff_7 (
    .J(or_10_out), .clk(CLOCK_out), .K(xor_4_out), .Q(Q7), .en(or_14_out), .reset(or_2_out));  // open: Qn, preset
  xor xor_4 (xor_4_out, M, Q8);
  or or_11 (or_11_out, and_18_out, and_19_out);
  not not_22 (not_22_out, HOLD_pin);
  and and_16 (and_16_out, or_12_out, M, not_23_out);
  not not_23 (not_23_out, Q8);
  not not_24 (not_24_out, M);
  and and_17 (and_17_out, Q8, not_24_out, not_25_out);
  not not_25 (not_25_out, Q5);
  Clock CLOCK (.out(CLOCK_out));
  not not_26 (not_26_out, Q7);
  and and_18 (and_18_out, Q8, not_26_out, not_27_out, not_28_out, Q5);
  not not_27 (not_27_out, M);
  not not_28 (not_28_out, Q6);
  not not_29 (not_29_out, Q8);
  not not_30 (not_30_out, Q7);
  and and_19 (and_19_out, not_29_out, not_30_out, M, not_31_out, not_32_out);
  not not_31 (not_31_out, Q6);
  not not_32 (not_32_out, Q5);
  or or_12 (or_12_out, Q6, Q5);
  J_K_Flip_Flop j_k_ff_8 (
    .J(1'b1), .clk(CLOCK_out), .K(1'b1), .Q(Q8), .preset(PRESET), .en(or_14_out), .reset(CLEAR));  // open: Qn
  Hex_Digit_Display hex_digit_display_2 (.value({Q5, Q6, Q7, Q8}));  // open: dp
  or or_13 (or_13_out, and_20_out, and_21_out);
  xor xor_5 (xor_5_out, M, Q12);
  or or_14 (or_14_out, and_26_out, and_27_out);
  not not_33 (not_33_out, M);
  and and_20 (and_20_out, not_33_out, Q10, Q11, Q12);
  not not_34 (not_34_out, Q10);
  and and_21 (and_21_out, M, not_34_out, not_35_out, not_36_out);
  not not_35 (not_35_out, Q11);
  not not_36 (not_36_out, Q12);
  J_K_Flip_Flop j_k_ff_9 (
    .J(or_13_out), .clk(CLOCK_out), .K(xor_5_out), .Q(Q9), .preset(PRESET), .en(not_22_out), .reset(CLEAR));  // open: Qn
  or or_15 (or_15_out, and_22_out, and_23_out);
  or or_16 (or_16_out, and_24_out, and_25_out);
  J_K_Flip_Flop j_k_ff_10 (
    .J(or_15_out), .clk(CLOCK_out), .K(or_16_out), .Q(Q10), .en(not_22_out), .reset(or_2_out));  // open: Qn, preset
  not not_37 (not_37_out, M);
  and and_22 (and_22_out, not_37_out, Q11, Q12);
  and and_23 (and_23_out, M, Q9, not_38_out);
  not not_38 (not_38_out, Q12);
  not not_39 (not_39_out, M);
  and and_24 (and_24_out, not_39_out, Q11, Q12);
  not not_40 (not_40_out, Q11);
  and and_25 (and_25_out, M, not_40_out, not_41_out);
  not not_41 (not_41_out, Q12);
  not not_42 (not_42_out, Q11);
  not not_43 (not_43_out, M);
  and and_26 (and_26_out, Q12, not_42_out, not_43_out, not_44_out, Q9, not_22_out);
  not not_44 (not_44_out, Q10);
  not not_45 (not_45_out, Q12);
  not not_46 (not_46_out, Q11);
  and and_27 (and_27_out, not_22_out, not_45_out, not_46_out, M, not_47_out, not_48_out);
  not not_47 (not_47_out, Q10);
  not not_48 (not_48_out, Q9);
  or or_17 (or_17_out, and_28_out, and_29_out);
  J_K_Flip_Flop j_k_ff_11 (
    .J(or_17_out), .clk(CLOCK_out), .K(xor_6_out), .Q(Q11), .en(not_22_out), .reset(or_2_out));  // open: Qn, preset
  xor xor_6 (xor_6_out, M, Q12);
  and and_28 (and_28_out, or_18_out, M, not_49_out);
  not not_49 (not_49_out, Q12);
  not not_50 (not_50_out, M);
  and and_29 (and_29_out, Q12, not_50_out, not_51_out);
  not not_51 (not_51_out, Q9);
  J_K_Flip_Flop j_k_ff_12 (
    .J(1'b1), .clk(CLOCK_out), .K(1'b1), .Q(Q12), .preset(PRESET), .en(not_22_out), .reset(CLEAR));  // open: Qn
  or or_18 (or_18_out, Q10, Q9);
  Hex_Digit_Display hex_digit_display_3 (.value({Q9, Q10, Q11, Q12}));  // open: dp

  // Notes on the sheet:
  //   Hundreds digit
  //   Tens digit
  //   Ones digit
endmodule

module decoder_for_mode_select (
  input  I1,
  input  I2,
  input  I3,
  output O1,
  output O2,
  output O3,
  output O4
);

  wire not_1_out, not_2_out, not_3_out;

  not not_1 (not_1_out, I2);
  not not_2 (not_2_out, I1);
  not not_3 (not_3_out, I3);
  and and_1 (O1, I1, not_1_out);
  and and_2 (O2, not_2_out, I2, I3);
  and and_3 (O3, not_2_out, I2, not_3_out);
  and and_4 (O4, not_1_out, I3);
endmodule

module ROM (
  input  in_1
);

  wire button_1_out, clock_1_out, comparator_1_lt, controlled_buffer_1_out, nor_1_out, not_1_out,
       register_1_q;
  wire [6:0] bit_extender_1_out, counter_1_q;
  wire [7:0] rom_1_data;

  Clock clock_1 (.out(clock_1_out));
  Button button_1 (.out(button_1_out));
  not not_1 (not_1_out, nor_1_out);
  Counter #(.width(7), .max('h7f)) counter_1 (
    .Q(counter_1_q), .clk(controlled_buffer_1_out), .clr(register_1_q));  // open: load, D, count, carry
  assign controlled_buffer_1_out = not_1_out ? clock_1_out : 1'bz;  // Controlled_Buffer controlled_buffer_1
  Register #(.width(1)) register_1 (
    .D(button_1_out), .Q(register_1_q), .clk(button_1_out), .clr(comparator_1_lt));  // open: en
  Comparator #(.width(1)) comparator_1 (.a(register_1_q), .b(1'b0), .lt(comparator_1_lt));  // open: gt, eq
  nor nor_1 (nor_1_out, rom_1_data[4], rom_1_data[7], rom_1_data[6], rom_1_data[5], rom_1_data[3], rom_1_data[2], rom_1_data[1], rom_1_data[0]);
  Bit_Extender #(.out_width(7), .\type ("one")) bit_extender_1 (.in(rom_1_data), .out(bit_extender_1_out));
  ROM_part #(.addrWidth(7)) rom_1 (.addr(counter_1_q), .data(rom_1_data));  // open: sel
  TTY #(.rows(20), .cols(40)) tty_1 (.data(bit_extender_1_out), .clk(controlled_buffer_1_out), .clr(in_1));  // open: we

  // Notes on the sheet:
  //   contents of rom_1 (hex, n*v repeats v):
  //   68 65 6c 6c 6f 20 77 6f 72 6c 64 21 20
endmodule
